# Fritzing sketch Circuitdiag (saved by Fritzing 0.9.4)
breadboards: 1

parts:
  Part1 = Arduino Uno (Rev3)
  LCD1 = LCD screen
  T1 = LM35 Temperature Sensor [package="TO92 [THT]"]
  SEN1 = Pulse Sensor [package=SIP]  # not connected
  U1 = ESP8266 WiFi Module [part_number=ESP8266]
  R1 = Resistor [tolerance=±5% resistance=220 package=THT]

nets:
  N1: Part1.A1, T1.Vout
  N2: Part1.D8, LCD1.RS
  N3: Part1.D9_PWM, LCD1.E
  N4: Part1.D10_PWM/SS, LCD1.DB4
  N5: Part1.D11_PWM/MOSI, LCD1.DB5
  N6: Part1.D12/MISO, LCD1.DB6
  N7: Part1.D13/SCK, LCD1.DB7
  N8: Part1.D2, U1.TXD
  N9: Part1.D3_PWM, U1.RXD
  N10: Part1.3V3, U1.CH_PD
  N11: Part1.5V, T1.+Vs
  GND: Part1.GND, T1.GND
  N12: U1.RST, R1.Pin_0

custom parts:
  Pulse Sensor: Pulse Sensor Optical Heart Rate Monitor for Arduino and other microcontrollers
  ESP8266 WiFi Module: Generic WiFi Module based on the ESP8266 with onboard PCB antenna and UART communications
